# Fritzing sketch Lamp (saved by Fritzing 0.9.3b)
circuit board: 8.46667cm x 5.64444cm

parts:
  Bauteil1 = Arduino Pro Mini (5V)
  U1 = ESP8266 WiFi Module [part_number=ESP8266]
  Bauteil2 = Logic Level Converter
  U2 = LIPO-110mAh [package=lipo-110]
  Bauteil3 = Power Cell LiPo Charger/Booster
  LM1 = RioRand LM2596
  LM2 = RioRand LM2596
  NEOPIXEL1 = Neopixel Strip -- Black (30/m)

nets:
  N1: Bauteil1.TXO, Bauteil2.TX2_HV
  N2: Bauteil1.RXI, Bauteil2.RX2_HV
  GND: Bauteil1.GND, U1.GND, Bauteil2.GND, LM1.Pin_3, LM2.Pin_3, NEOPIXEL1.GND
  VCC: Bauteil1.VCC, Bauteil2.HV, LM1.Pin_2, NEOPIXEL1.+5V
  N3: Bauteil1.D9, NEOPIXEL1.Din
  N4: U1.RXD, Bauteil2.RX2_LV
  N5: U1.VCC, U1.CH_PD, Bauteil2.LV, LM2.Pin_2
  N6: U1.TXD, Bauteil2.TX2_LV
  N7: U2.+, Bauteil3.VCC
  N8: U2.-, Bauteil3.GND

notes:
  5V -> 3,3V
  LiPo -> 5V
  Charger

custom parts:
  ESP8266 WiFi Module: Generic WiFi Module based on the ESP8266 with onboard PCB antenna and UART communications
  Neopixel Strip -- Black (30/m): These NeoPixel strips have 30 digitally-addressable pixel LEDs per meter and are very affordable and are only 12.5 mm wide, 10 mm if you remove the strip from the casing.
